# Fritzing sketch OpenChrono_LiPo (saved by Fritzing 0.9.10b)

parts:
  U1 = Arduino Nano (Rev3.0)
  LED1 = LED - 3mm [color="Infrared (940nm)" current=20mA package="3 mm [THT]"]
  LED2 = LED - 3mm [color="Infrared (940nm)" current=0.030 package="3 mm [THT]"]
  LED3 = LED - 3mm [color="White (4500K)" current=0.030 package="3 mm [THT]"]
  LED4 = LED - 3mm [color="White (4500K)" current=30mA package="3 mm [THT]"]
  R1 = Resistor [tolerance=±5% power=0.25 resistance=1k package=THT]
  R2 = Resistor [tolerance=±5% power=0.25 resistance=1k package=THT]
  R3 = Resistor [tolerance=±5% power=0.25 resistance=100 package=THT]
  R4 = Resistor [tolerance=±5% power=0.25 resistance=100 package=THT]
  U2 = OLED 128x64 I2C Monochrome Display
  Q1 = LTR-301 [package=ltr-301]
  Q2 = LTR-301 [package=ltr-301]
  S1 = SPST Switch [package=switch-spdt_lock.007s]
  U3 = LIPO-110mAh [package=lipo-110]
  TP1 = TP4056 [chip_label=TP4056 package="DIP (Dual Inline) [THT]"]

nets:
  GND: U1.GND, LED2.cathode, LED4.cathode, U2.GND, Q1.E, Q2.E, TP1.pin6
  N1: U1.D2, R1.Pin_0, Q1.C
  N2: U1.D3, R2.Pin_0, Q2.C
  N3: U1.D4, LED1.anode
  N4: U1.D5, LED3.anode
  5V: U1.5V, R1.Pin_1, R2.Pin_1, U2.VDD, S1.S
  N5: U1.A5, U2.SCK
  N6: U1.A4, U2.SDA
  N7: LED1.cathode, R3.Pin_1
  N8: LED2.anode, R3.Pin_0
  N9: LED3.cathode, R4.Pin_1
  N10: LED4.anode, R4.Pin_0
  N11: S1.P, TP1.pin3
  N12: U3.+, TP1.pin4
  N13: U3.-, TP1.pin5

notes:
  IR LEDs
  UV LEDs
  Phototransistors

custom parts:
  TP4056: A DIP stand-in part for whatever IC you want. With 6 pins on a 300mil dual inline package (DIP) footprint.
